// Logisim project Data-Memory.circ as structural Verilog: 1 circuit, main circuit Data Memory
module Data_Memory (
  input  [7:0] Address,
  input  [7:0] Write_Data,
  input  Mem_Write,
  input  Mem_Read,
  input  Clear,
  input  CLK,
  output [7:0] Data
);

  wire not_1_out;

  not not_1 (not_1_out, CLK);
  RAM #(.bus("separate")) ram_1 (
    .addr(Address), .din(Write_Data), .data(Data), .str(Mem_Write), .clk(not_1_out), .ld(Mem_Read),
    .clr(Clear));  // open: sel
endmodule
