// Logisim project HazardControl.circ as structural Verilog: 2 circuits, main circuit Forwarding Unit
module Forwarding_Unit (
  input  EX_MEM_Reg_Write,
  input  [3:0] ID_EX_Src_Reg_1,
  input  MEM_WB_Reg_Write,
  input  [3:0] ID_EX_Src_Reg_2,
  input  [3:0] EX_MEM_Dest_Reg,
  input  [3:0] MEM_WB_Dest_Reg,
  output [1:0] Forward_A,
  output [1:0] Forward_B
);

  wire and_1_out, and_3_out, comparator_3_eq, comparator_4_eq, EX_MEM_Dest_Reg____0,
       ID_EX_SrcReg1____EX_MEM_DestReg, ID_EX_SrcReg1____MEM_WB_DestReg, ID_EX_SrcReg2____EX_MEM_DestReg,
       ID_EX_SrcReg2____MEM_WB_DestReg, MEM_WB_Dest_Reg____0, not_3_out, not_4_out;

  Comparator #(.width(4)) comparator_1 (
    .a(MEM_WB_Dest_Reg), .b(ID_EX_Src_Reg_1), .eq(ID_EX_SrcReg1____MEM_WB_DestReg));  // open: gt, lt
  Comparator #(.width(4)) comparator_2 (
    .a(ID_EX_Src_Reg_1), .b(EX_MEM_Dest_Reg), .eq(ID_EX_SrcReg1____EX_MEM_DestReg));  // open: gt, lt
  Comparator #(.width(4)) comparator_3 (.a(MEM_WB_Dest_Reg), .b(4'b0000), .eq(comparator_3_eq));  // open: gt, lt
  Comparator #(.width(4)) comparator_4 (.a(EX_MEM_Dest_Reg), .b(4'b0000), .eq(comparator_4_eq));  // open: gt, lt
  Comparator #(.width(4)) comparator_5 (
    .a(EX_MEM_Dest_Reg), .b(ID_EX_Src_Reg_2), .eq(ID_EX_SrcReg2____EX_MEM_DestReg));  // open: gt, lt
  Comparator #(.width(4)) comparator_6 (
    .a(MEM_WB_Dest_Reg), .b(ID_EX_Src_Reg_2), .eq(ID_EX_SrcReg2____MEM_WB_DestReg));  // open: gt, lt
  not not_1 (MEM_WB_Dest_Reg____0, comparator_3_eq);
  not not_2 (EX_MEM_Dest_Reg____0, comparator_4_eq);
  not not_3 (not_3_out, Forward_B[1]);
  and and_1 (and_1_out, ID_EX_SrcReg1____EX_MEM_DestReg, EX_MEM_Dest_Reg____0);
  not not_4 (not_4_out, Forward_A[1]);
  and and_2 (Forward_B[0], not_3_out, ID_EX_SrcReg2____MEM_WB_DestReg, MEM_WB_Dest_Reg____0, MEM_WB_Reg_Write);
  and and_3 (and_3_out, EX_MEM_Dest_Reg____0, ID_EX_SrcReg2____EX_MEM_DestReg);
  and and_4 (Forward_A[1], EX_MEM_Reg_Write, and_1_out);
  and and_5 (Forward_A[0], not_4_out, ID_EX_SrcReg1____MEM_WB_DestReg, MEM_WB_Dest_Reg____0, MEM_WB_Reg_Write);
  and and_6 (Forward_B[1], EX_MEM_Reg_Write, and_3_out);
endmodule

module Hazard_Detection (
  input  [3:0] IF_ID_rs,
  input  [3:0] ID_EX_rt,
  input  [3:0] IF_ID_rt,
  input  ID_EX_MemRead,
  output LW_Hazard_Detected
);

  wire IF_ID_rs____ID_EX_rt, IF_ID_rt____ID_EX_rt, or_1_out;

  Comparator #(.width(4)) comparator_1 (.a(IF_ID_rs), .b(ID_EX_rt), .eq(IF_ID_rs____ID_EX_rt));  // open: gt, lt
  Comparator #(.width(4)) comparator_2 (.a(ID_EX_rt), .b(IF_ID_rt), .eq(IF_ID_rt____ID_EX_rt));  // open: gt, lt
  or or_1 (or_1_out, IF_ID_rs____ID_EX_rt, IF_ID_rt____ID_EX_rt);
  and and_1 (LW_Hazard_Detected, ID_EX_MemRead, or_1_out);
endmodule
