// Logisim project PipelineReg.circ as structural Verilog: 4 circuits, main circuit IF/ID
module IF_ID (
  input  [7:0] PC_in,
  input  [19:0] Instruction_in,
  input  WRITE,
  input  CLK,
  input  CLR,
  output [7:0] PC_out,
  output [19:0] Instruction_Out
);

  wire not_1_out;

  not not_1 (not_1_out, WRITE);
  Register register_1 (.D(PC_in), .en(not_1_out), .Q(PC_out), .clk(CLK), .clr(CLR));
  Register #(.width(20)) register_2 (.D(Instruction_in), .en(not_1_out), .Q(Instruction_Out), .clk(CLK), .clr(CLR));
endmodule

module ID_EX (
  input  CLK,
  input  ALUSrc_in,
  input  CLR,
  input  Stall,
  input  MemtoReg_in,
  input  RegWrite_in,
  input  [7:0] PC_in,
  input  RegDst_in,
  input  [3:0] RS_in,
  input  [3:0] RT_in,
  input  MemWrite_in,
  input  [2:0] ALUOp_in,
  input  MemRead_in,
  input  [3:0] DstReg_in,
  input  [7:0] Address_Immediate_in,
  input  [7:0] ShiftAmount_in,
  input  Shift_in,
  input  [7:0] Read_Rs_in,
  input  [7:0] Read_Rt_in,
  output ALUSrc_out,
  output MemtoReg_out,
  output RegWrite_out,
  output [7:0] PC_out,
  output RegDst_out,
  output [3:0] RS_out,
  output [3:0] RT_out,
  output MemWrite_out,
  output [2:0] ALUOp_out,
  output MemRead_out,
  output [3:0] DstReg_out,
  output [7:0] Address_Immediate_out,
  output [7:0] ShiftAmount_out,
  output Shift_out,
  output [7:0] Read_Rs_out,
  output [7:0] Read_Rt_out
);

  wire multiplexer_2_out, multiplexer_3_out, multiplexer_4_out, multiplexer_5_out, multiplexer_6_out,
       multiplexer_7_out, multiplexer_8_out;
  wire [2:0] multiplexer_1_out;

  Multiplexer #(.width(3), .enable("false")) multiplexer_1 (
    .in0(ALUOp_in), .in1(3'b000), .out(multiplexer_1_out), .sel(Stall));
  Register #(.width(3)) ALU_OP (.D(multiplexer_1_out), .en(1'b1), .Q(ALUOp_out), .clk(CLK), .clr(CLR));
  Register #(.width(4)) DstReg (.D(DstReg_in), .en(1'b1), .Q(DstReg_out), .clk(CLK), .clr(CLR));
  Register PC (.D(PC_in), .en(1'b1), .Q(PC_out), .clk(CLK), .clr(CLR));
  Register #(.width(4)) RS (.D(RS_in), .en(1'b1), .Q(RS_out), .clk(CLK), .clr(CLR));
  Register #(.width(4)) RT (.D(RT_in), .en(1'b1), .Q(RT_out), .clk(CLK), .clr(CLR));
  Register ShiftAmount (.D(ShiftAmount_in), .en(1'b1), .Q(ShiftAmount_out), .clk(CLK), .clr(CLR));
  Register Read_Rs (.D(Read_Rs_in), .en(1'b1), .Q(Read_Rs_out), .clk(CLK), .clr(CLR));
  Register Read_Rt (.D(Read_Rt_in), .en(1'b1), .Q(Read_Rt_out), .clk(CLK), .clr(CLR));
  Multiplexer #(.enable("false")) multiplexer_2 (.in0(ALUSrc_in), .in1(1'b0), .out(multiplexer_2_out), .sel(Stall));
  Multiplexer #(.enable("false")) multiplexer_3 (.in0(MemtoReg_in), .in1(1'b0), .out(multiplexer_3_out), .sel(Stall));
  Multiplexer #(.enable("false")) multiplexer_4 (.in0(RegWrite_in), .in1(1'b0), .out(multiplexer_4_out), .sel(Stall));
  Multiplexer #(.enable("false")) multiplexer_5 (.in0(RegDst_in), .in1(1'b0), .out(multiplexer_5_out), .sel(Stall));
  Multiplexer #(.enable("false")) multiplexer_6 (.in0(MemWrite_in), .in1(1'b0), .out(multiplexer_6_out), .sel(Stall));
  Multiplexer #(.enable("false")) multiplexer_7 (.in0(MemRead_in), .in1(1'b0), .out(multiplexer_7_out), .sel(Stall));
  Multiplexer #(.enable("false")) multiplexer_8 (.in0(Shift_in), .in1(1'b0), .out(multiplexer_8_out), .sel(Stall));
  Register #(.width(1)) ALUSrc (.D(multiplexer_2_out), .en(1'b1), .Q(ALUSrc_out), .clk(CLK), .clr(CLR));
  Register #(.width(1)) MemtoReg (.D(multiplexer_3_out), .en(1'b1), .Q(MemtoReg_out), .clk(CLK), .clr(CLR));
  Register #(.width(1)) RegWrite (.D(multiplexer_4_out), .en(1'b1), .Q(RegWrite_out), .clk(CLK), .clr(CLR));
  Register #(.width(1)) RegDst (.D(multiplexer_5_out), .en(1'b1), .Q(RegDst_out), .clk(CLK), .clr(CLR));
  Register #(.width(1)) MemWrite (.D(multiplexer_6_out), .en(1'b1), .Q(MemWrite_out), .clk(CLK), .clr(CLR));
  Register #(.width(1)) MemRead (.D(multiplexer_7_out), .en(1'b1), .Q(MemRead_out), .clk(CLK), .clr(CLR));
  Register #(.width(1)) Shift (.D(multiplexer_8_out), .en(1'b1), .Q(Shift_out), .clk(CLK), .clr(CLR));
  Register Address_Immediate (.D(Address_Immediate_in), .en(1'b1), .Q(Address_Immediate_out), .clk(CLK), .clr(CLR));
endmodule

module EX_MEM (
  input  MemtoReg_in,
  input  CLK,
  input  CLR,
  input  RegWrite_in,
  input  [7:0] PC_in,
  input  StoreStack_in,
  input  [3:0] DstReg_in,
  input  MemWrite_in,
  input  [3:0] RT_in,
  input  MemRead_in,
  input  [7:0] Write_Data_in,
  input  [7:0] ALUResult_in,
  output MemtoReg_out,
  output RegWrite_out,
  output [7:0] PC_out,
  output StoreStack_out,
  output [3:0] DstReg_out,
  output MemWrite_out,
  output [3:0] RT_out,
  output MemRead_out,
  output [7:0] Write_Data_out,
  output [7:0] ALUResult_out
);

  Register PC (.D(PC_in), .en(1'b1), .Q(PC_out), .clk(CLK), .clr(CLR));
  Register #(.width(4)) DstReg (.D(DstReg_in), .en(1'b1), .Q(DstReg_out), .clk(CLK), .clr(CLR));
  Register #(.width(4)) RT (.D(RT_in), .en(1'b1), .Q(RT_out), .clk(CLK), .clr(CLR));
  Register ALUResult (.D(ALUResult_in), .en(1'b1), .Q(ALUResult_out), .clk(CLK), .clr(CLR));
  Register #(.width(1)) MemtoReg (.D(MemtoReg_in), .en(1'b1), .Q(MemtoReg_out), .clk(CLK), .clr(CLR));
  Register #(.width(1)) RegWrite (.D(RegWrite_in), .en(1'b1), .Q(RegWrite_out), .clk(CLK), .clr(CLR));
  Register #(.width(1)) StoreStack (.D(StoreStack_in), .en(1'b1), .Q(StoreStack_out), .clk(CLK), .clr(CLR));
  Register #(.width(1)) MemWrite (.D(MemWrite_in), .en(1'b1), .Q(MemWrite_out), .clk(CLK), .clr(CLR));
  Register #(.width(1)) MemRead (.D(MemRead_in), .en(1'b1), .Q(MemRead_out), .clk(CLK), .clr(CLR));
  Register Write_Data (.D(Write_Data_in), .en(1'b1), .Q(Write_Data_out), .clk(CLK), .clr(CLR));
endmodule

module MEM_WB (
  input  CLK,
  input  CLR,
  input  [7:0] PC_in,
  input  MemtoReg_in,
  input  RegWrite_in,
  input  [3:0] RT_in,
  input  [3:0] Destination_Reg_in,
  input  [7:0] Read_Data_in,
  input  [7:0] ALUResult_in,
  output [7:0] PC_out,
  output MemtoReg_out,
  output RegWrite_out,
  output [3:0] RT_out,
  output [3:0] Destination_Reg_out,
  output [7:0] Read_Data_out,
  output [7:0] ALUResult_out
);

  Register PC (.D(PC_in), .en(1'b1), .Q(PC_out), .clk(CLK), .clr(CLR));
  Register #(.width(4)) RT (.D(RT_in), .en(1'b1), .Q(RT_out), .clk(CLK), .clr(CLR));
  Register #(.width(4)) Destination_Reg (
    .D(Destination_Reg_in), .en(1'b1), .Q(Destination_Reg_out), .clk(CLK), .clr(CLR));
  Register ALUResult (.D(ALUResult_in), .en(1'b1), .Q(ALUResult_out), .clk(CLK), .clr(CLR));
  Register #(.width(1)) MemtoReg (.D(MemtoReg_in), .en(1'b1), .Q(MemtoReg_out), .clk(CLK), .clr(CLR));
  Register #(.width(1)) RegWrite (.D(RegWrite_in), .en(1'b1), .Q(RegWrite_out), .clk(CLK), .clr(CLR));
  Register Read_Data (.D(Read_Data_in), .en(1'b1), .Q(Read_Data_out), .clk(CLK), .clr(CLR));
endmodule
