// Logisim project PipelinedMIPS.circ as structural Verilog: 3 circuits, main circuit main
module main (
  input  Reset
);

  wire and_1_out, and_2_out, and_3_out, and_4_out, Branch_Hazard, Clock, EX_MEM_MemRead, EX_MEM_MemToReg,
       EX_MEM_MemWrite, EX_MEM_RegWrite, EX_MEM_StoreStack, ID_EX_ALUSrc, ID_EX_MemRead, ID_EX_MemToReg,
       ID_EX_MemWrite, ID_EX_RegDst, ID_EX_RegWrite, ID_EX_Shift, ID_EX_StoreStack, IF_ID_ALUSrc, IF_ID_Beq,
       IF_ID_Bne, IF_ID_Jump, IF_ID_MemRead, IF_ID_MemToReg, IF_ID_MemWrite, IF_ID_RegDst, IF_ID_RegWrite,
       IF_ID_Shift, Load_Use_Hazard, MEM_WB_MemToReg, MEM_WB_RegWrite, not_1_out, or_2_out, PC_Src, Stall;
  wire [1:0] Branch_Data_Forward_A, Branch_Data_Forward_B, Data_Forward_A, Data_Forward_B, multiplexer_4_out,
       multiplexer_5_out, multiplexer_12_out;
  wire [2:0] ID_EX_ALUOp, IF_ID_ALUOp;
  wire [3:0] EX_MEM_DstReg, EX_MEM_Source_Register_2, ID_EX_DstReg, ID_EX_New_DstReg,
       ID_EX_Source_Register_1, ID_EX_Source_Register_2, IF_ID_DstReg, IF_ID_OpCode, IF_ID_ShiftAmount,
       IF_ID_Source_Register_1, IF_ID_Source_Register_2, MEM_WB_DstReg, MEM_WB_Source_Register_2;
  wire [7:0] ALU_B, ALU_Result, EX_MEM_ALU_Result, EX_MEM_New_Read_Data, EX_MEM_PC, EX_MEM_Read_Memory_Data,
       EX_MEM_Read_Stack_Data, EX_MEM_WriteData, Final_PC, Forwarded_ALU_A, Forwarded_ALU_B,
       ID_EX_Address_Immediate, ID_EX_New_ShiftAmount, ID_EX_PC, ID_EX_Read_Register_1,
       ID_EX_Read_Register_2, ID_EX_WriteData, IF_ID_Address_Immediate, IF_ID_JumpAddress,
       IF_ID_New_ShiftAmount, IF_ID_PC, IF_ID_Read_Data_1, IF_ID_Read_Data_2, IF_ID_Read_Register_1,
       IF_ID_Read_Register_2, MEM_WB_ALU_Result, MEM_WB_PC, MEM_WB_Read_Data, MEM_WB_WriteData,
       multiplexer_8_out, multiplexer_9_out, New_PC, Old_PC, Old_PC___1;
  wire [19:0] IF_ID_Ins, Instruction;

  Clock u_Clock (.out(Clock));
  Multiplexer #(.width(8), .enable("false")) multiplexer_1 (
    .in0(Old_PC___1), .in1(New_PC), .out(Final_PC), .sel(PC_Src));
  Instruction_Memory instruction_memory_1 (
    .PC_input(Final_PC), .Clock(Clock), .Instruction(Instruction), .PC_Out(Old_PC), .PC_Src(PC_Src),
    .Reset(Reset), .Stall(Stall));
  or or_1 (Stall, Load_Use_Hazard, Branch_Hazard);
  Adder adder_1 (.a(Old_PC), .b(8'h1), .out(Old_PC___1));  // open: cin, cout
  IF_ID if_id_1 (
    .PC_in(Old_PC___1), .Instruction_in(Instruction), .PC_out(IF_ID_PC), .Instruction_Out(IF_ID_Ins),
    .WRITE(Stall), .CLK(Clock), .CLR(Reset));
  insSplitter inssplitter_1 (
    .in_1(IF_ID_Ins), .Shift_Amount(IF_ID_ShiftAmount), .Dst_Reg(IF_ID_DstReg),
    .Src_Reg2(IF_ID_Source_Register_2), .Src_Reg1(IF_ID_Source_Register_1), .Opcode(IF_ID_OpCode),
    .Address_Immediate(IF_ID_Address_Immediate), .Target_Jump_Address(IF_ID_JumpAddress));
  Control_Unit control_unit_1 (
    .Opcode(IF_ID_OpCode), .Shift(IF_ID_Shift), .ALU_Op(IF_ID_ALUOp), .Reg_Dest(IF_ID_RegDst),
    .ALU_Src(IF_ID_ALUSrc), .MemToReg(IF_ID_MemToReg), .RegWrite(IF_ID_RegWrite), .beq(IF_ID_Beq),
    .bneq(IF_ID_Bne), .MemWrite(IF_ID_MemWrite), .MemRead(IF_ID_MemRead), .Jump(IF_ID_Jump));
  control_hazard control_hazard_1 (
    .bne(IF_ID_Bne), .EX_MEM_Rt(EX_MEM_Source_Register_2), .IF_ID_Rs(IF_ID_Source_Register_1),
    .ID_EX_Rd(ID_EX_New_DstReg), .IF_ID_Rt(IF_ID_Source_Register_2), .beq(IF_ID_Beq),
    .EX_MEM_MemRead(EX_MEM_MemRead), .ID_EX_RegWrite(ID_EX_RegWrite), .jump_control(Branch_Hazard));
  Forwarding_Unit forwarding_unit_1 (
    .EX_MEM_Reg_Write(EX_MEM_RegWrite), .ID_EX_Src_Reg_1(IF_ID_Source_Register_1),
    .MEM_WB_Reg_Write(MEM_WB_RegWrite), .ID_EX_Src_Reg_2(IF_ID_Source_Register_2),
    .EX_MEM_Dest_Reg(EX_MEM_DstReg), .MEM_WB_Dest_Reg(MEM_WB_DstReg), .Forward_A(Branch_Data_Forward_A),
    .Forward_B(Branch_Data_Forward_B));
  assign IF_ID_New_ShiftAmount = {{4{1'b0}}, IF_ID_ShiftAmount};  // Bit_Extender bit_extender_1
  Next_PC_Calculation next_pc_calculation_1 (
    .Rt(IF_ID_Read_Data_1), .Beq(IF_ID_Beq), .Bne(IF_ID_Bne), .Branch_Target(IF_ID_Address_Immediate),
    .Jump(IF_ID_Jump), .Jump_Target(IF_ID_JumpAddress), .PC___1(IF_ID_PC), .New_PC(New_PC),
    .Rs(IF_ID_Read_Data_2), .PC_Src(PC_Src));
  Multiplexer #(.select(2), .width(8), .enable("false")) multiplexer_2 (
    .in0(IF_ID_Read_Register_1), .in1(MEM_WB_WriteData), .in2(EX_MEM_ALU_Result), .out(IF_ID_Read_Data_1),
    .sel(multiplexer_4_out));  // open: in3
  Multiplexer #(.select(2), .width(8), .enable("false")) multiplexer_3 (
    .in0(IF_ID_Read_Register_2), .in1(MEM_WB_WriteData), .in2(EX_MEM_ALU_Result), .out(IF_ID_Read_Data_2),
    .sel(multiplexer_5_out));  // open: in3
  Register_File register_file_1 (
    .Read_Register_1(IF_ID_Source_Register_1), .Read_Register_2(IF_ID_Source_Register_2),
    .Write_Register(MEM_WB_DstReg), .Write_Data(MEM_WB_WriteData), .Read_Data_1(IF_ID_Read_Register_1),
    .Read_Data_2(IF_ID_Read_Register_2), .Write_Signal(MEM_WB_RegWrite), .CLK(Clock), .Clear(Reset));
  Hazard_Detection hazard_detection_1 (
    .IF_ID_rs(IF_ID_Source_Register_1), .ID_EX_rt(ID_EX_Source_Register_2),
    .IF_ID_rt(IF_ID_Source_Register_2), .ID_EX_MemRead(ID_EX_MemRead), .LW_Hazard_Detected(Load_Use_Hazard));
  Multiplexer #(.width(2), .enable("false")) multiplexer_4 (
    .in0(2'b00), .in1(Branch_Data_Forward_A), .out(multiplexer_4_out), .sel(or_2_out));
  Multiplexer #(.width(2), .enable("false")) multiplexer_5 (
    .in0(2'b00), .in1(Branch_Data_Forward_B), .out(multiplexer_5_out), .sel(or_2_out));
  or or_2 (or_2_out, IF_ID_Beq, IF_ID_Bne);
  ID_EX id_ex_1 (
    .CLK(Clock), .ALUSrc_in(IF_ID_ALUSrc), .CLR(Reset), .MemtoReg_in(IF_ID_MemToReg),
    .RegWrite_in(IF_ID_RegWrite), .PC_in(IF_ID_PC), .MemWrite_in(IF_ID_MemWrite), .ALUOp_in(IF_ID_ALUOp),
    .MemRead_in(IF_ID_MemRead), .Shift_in(IF_ID_Shift), .ALUSrc_out(ID_EX_ALUSrc),
    .MemtoReg_out(ID_EX_MemToReg), .RegWrite_out(ID_EX_RegWrite), .PC_out(ID_EX_PC),
    .MemWrite_out(ID_EX_MemWrite), .ALUOp_out(ID_EX_ALUOp), .MemRead_out(ID_EX_MemRead),
    .Shift_out(ID_EX_Shift), .RS_in(IF_ID_Source_Register_1), .RS_out(ID_EX_Source_Register_1),
    .RT_in(IF_ID_Source_Register_2), .RT_out(ID_EX_Source_Register_2), .DstReg_in(IF_ID_DstReg),
    .DstReg_out(ID_EX_DstReg), .ShiftAmount_in(IF_ID_New_ShiftAmount),
    .ShiftAmount_out(ID_EX_New_ShiftAmount), .RegDst_in(IF_ID_RegDst), .RegDst_out(ID_EX_RegDst),
    .Read_Rs_in(IF_ID_Read_Data_1), .Read_Rs_out(ID_EX_Read_Register_1), .Read_Rt_in(IF_ID_Read_Data_2),
    .Read_Rt_out(ID_EX_Read_Register_2), .Address_Immediate_in(IF_ID_Address_Immediate),
    .Address_Immediate_out(ID_EX_Address_Immediate), .Stall(Stall));
  Multiplexer #(.width(4), .enable("false")) multiplexer_6 (
    .in0(ID_EX_Source_Register_2), .in1(ID_EX_DstReg), .out(ID_EX_New_DstReg), .sel(ID_EX_RegDst));
  Multiplexer #(.select(2), .width(8), .enable("false")) multiplexer_7 (
    .in0(multiplexer_9_out), .in1(ID_EX_Read_Register_2), .in2(ID_EX_Read_Register_1), .out(Forwarded_ALU_B),
    .sel({ID_EX_Shift, ID_EX_MemWrite}));  // open: in3
  Forwarding_Unit forwarding_unit_2 (
    .EX_MEM_Reg_Write(EX_MEM_RegWrite), .ID_EX_Src_Reg_1(ID_EX_Source_Register_1),
    .MEM_WB_Reg_Write(MEM_WB_RegWrite), .ID_EX_Src_Reg_2(ID_EX_Source_Register_2),
    .EX_MEM_Dest_Reg(EX_MEM_DstReg), .MEM_WB_Dest_Reg(MEM_WB_DstReg), .Forward_A(Data_Forward_A),
    .Forward_B(Data_Forward_B));
  Multiplexer #(.width(8), .enable("false")) multiplexer_8 (
    .in0(Forwarded_ALU_A), .in1(ID_EX_New_ShiftAmount), .out(multiplexer_8_out), .sel(ID_EX_Shift));
  Multiplexer #(.select(2), .width(8), .enable("false")) multiplexer_9 (
    .in0(ID_EX_Read_Register_2), .in1(ID_EX_Address_Immediate), .in2(ID_EX_Read_Register_1),
    .out(multiplexer_9_out), .sel({ID_EX_Shift, ID_EX_ALUSrc}));  // open: in3
  Multiplexer #(.select(2), .width(8), .enable("false")) multiplexer_10 (
    .in0(ID_EX_Read_Register_1), .in1(MEM_WB_WriteData), .in2(EX_MEM_ALU_Result), .out(Forwarded_ALU_A),
    .sel(Data_Forward_A));  // open: in3
  Multiplexer #(.select(2), .width(8), .enable("false")) multiplexer_11 (
    .in0(Forwarded_ALU_B), .in1(MEM_WB_WriteData), .in2(EX_MEM_ALU_Result), .out(ID_EX_WriteData),
    .sel(multiplexer_12_out));  // open: in3
  Multiplexer #(.width(2), .enable("false")) multiplexer_12 (
    .in0(Data_Forward_B), .in1(Data_Forward_A), .out(multiplexer_12_out), .sel(ID_EX_Shift));
  Stack_Logic stack_logic_1 (.Source_Reg_1(ID_EX_Source_Register_1), .Store_Stack(ID_EX_StoreStack));
  // ALU_8_by_ART alu_8_by_art_1: pin names not known; wires that end beside it: multiplexer_8_out, ALU_B, ID_EX_ALUOp, ALU_Result
  Multiplexer #(.width(8), .enable("false")) multiplexer_13 (
    .in0(ID_EX_WriteData), .in1(multiplexer_9_out), .out(ALU_B), .sel(ID_EX_MemWrite));
  EX_MEM ex_mem_1 (
    .MemtoReg_in(ID_EX_MemToReg), .CLK(Clock), .CLR(Reset), .RegWrite_in(ID_EX_RegWrite), .PC_in(ID_EX_PC),
    .MemWrite_in(ID_EX_MemWrite), .MemRead_in(ID_EX_MemRead), .Write_Data_in(ID_EX_WriteData),
    .ALUResult_in(ALU_Result), .MemtoReg_out(EX_MEM_MemToReg), .RegWrite_out(EX_MEM_RegWrite),
    .PC_out(EX_MEM_PC), .MemWrite_out(EX_MEM_MemWrite), .MemRead_out(EX_MEM_MemRead),
    .Write_Data_out(EX_MEM_WriteData), .ALUResult_out(EX_MEM_ALU_Result), .DstReg_in(ID_EX_New_DstReg),
    .DstReg_out(EX_MEM_DstReg), .StoreStack_in(ID_EX_StoreStack), .StoreStack_out(EX_MEM_StoreStack),
    .RT_in(ID_EX_Source_Register_2), .RT_out(EX_MEM_Source_Register_2));
  and and_1 (and_1_out, EX_MEM_MemRead, EX_MEM_StoreStack);
  and and_2 (and_2_out, EX_MEM_StoreStack, EX_MEM_MemWrite);
  Stack_Memory stack_memory_1 (
    .Address(EX_MEM_ALU_Result), .Write_Data(EX_MEM_WriteData), .Mem_Write(and_2_out), .Mem_Read(and_1_out),
    .Clear(Reset), .Data(EX_MEM_Read_Stack_Data), .CLK(Clock));
  and and_3 (and_3_out, EX_MEM_MemRead, not_1_out);
  not not_1 (not_1_out, EX_MEM_StoreStack);
  and and_4 (and_4_out, not_1_out, EX_MEM_MemWrite);
  Data_Memory data_memory_1 (
    .Address(EX_MEM_ALU_Result), .Write_Data(EX_MEM_WriteData), .Mem_Write(and_4_out), .Mem_Read(and_3_out),
    .Clear(Reset), .Data(EX_MEM_Read_Memory_Data), .CLK(Clock));
  Multiplexer #(.width(8), .enable("false")) multiplexer_14 (
    .in0(EX_MEM_Read_Memory_Data), .in1(EX_MEM_Read_Stack_Data), .out(EX_MEM_New_Read_Data),
    .sel(EX_MEM_StoreStack));
  MEM_WB mem_wb_1 (
    .CLK(Clock), .CLR(Reset), .PC_in(EX_MEM_PC), .MemtoReg_in(EX_MEM_MemToReg),
    .RegWrite_in(EX_MEM_RegWrite), .Destination_Reg_in(EX_MEM_DstReg), .Read_Data_in(EX_MEM_New_Read_Data),
    .ALUResult_in(EX_MEM_ALU_Result), .PC_out(MEM_WB_PC), .MemtoReg_out(MEM_WB_MemToReg),
    .RegWrite_out(MEM_WB_RegWrite), .Destination_Reg_out(MEM_WB_DstReg), .Read_Data_out(MEM_WB_Read_Data),
    .ALUResult_out(MEM_WB_ALU_Result), .RT_in(EX_MEM_Source_Register_2), .RT_out(MEM_WB_Source_Register_2));
  Multiplexer #(.width(8), .enable("false")) multiplexer_15 (
    .in0(MEM_WB_ALU_Result), .in1(MEM_WB_Read_Data), .out(MEM_WB_WriteData), .sel(MEM_WB_MemToReg));
endmodule

module Next_PC_Calculation (
  input  [7:0] Rs,
  input  [7:0] Rt,
  input  Beq,
  input  Bne,
  input  [7:0] Branch_Target,
  input  Jump,
  input  [7:0] Jump_Target,
  input  [7:0] PC___1,
  output [7:0] New_PC,
  output PC_Src
);

  wire Branch, Zero;
  wire [7:0] and_1_out, and_2_out, bit_extender_1_out, bit_extender_2_out, New_Branch_Target;

  Comparator comparator_1 (.a(Rs), .b(Rt), .eq(Zero));  // open: gt, lt
  Multiplexer #(.enable("false")) multiplexer_1 (.in0(Bne), .in1(Beq), .out(Branch), .sel(Zero));
  Adder adder_1 (.a(Branch_Target), .b(PC___1), .out(New_Branch_Target));  // open: cin, cout
  assign bit_extender_1_out = {{7{Branch}}, Branch};  // Bit_Extender bit_extender_1
  assign bit_extender_2_out = {{7{Jump}}, Jump};  // Bit_Extender bit_extender_2
  assign and_1_out = New_Branch_Target & bit_extender_1_out;  // AND_Gate and_1, 8 bits wide
  assign and_2_out = Jump_Target & bit_extender_2_out;  // AND_Gate and_2, 8 bits wide
  or or_1 (PC_Src, Branch, Jump);
  assign New_PC = and_1_out | and_2_out;  // OR_Gate or_2, 8 bits wide
endmodule

module Register_File (
  input  [3:0] Read_Register_1,
  input  [3:0] Read_Register_2,
  input  [3:0] Write_Register,
  input  [7:0] Write_Data,
  input  Write_Signal,
  input  CLK,
  input  Clear,
  output [7:0] Read_Data_1,
  output [7:0] Read_Data_2
);

  wire and_1_out, and_2_out, and_3_out, and_4_out, and_5_out, and_6_out, and_7_out, and_8_out, and_9_out,
       and_10_out, comparator_1_eq, comparator_2_eq, decoder_1_out0, decoder_1_out1, decoder_1_out2,
       decoder_1_out3, decoder_1_out4, decoder_1_out5, decoder_1_out6, decoder_1_out7, multiplexer_1_out,
       multiplexer_3_out;
  wire [7:0] multiplexer_2_out, multiplexer_4_out, multiplexer_5_out, sp_q, t0_q, t1_q, t2_q, t3_q, t4_q,
       t5_q, zero_q;

  Decoder #(.select(4), .enable("false")) decoder_1 (
    .out0(decoder_1_out0), .out1(decoder_1_out1), .out2(decoder_1_out2), .out3(decoder_1_out3),
    .out4(decoder_1_out4), .out5(decoder_1_out5), .out6(decoder_1_out6), .out7(decoder_1_out7),
    .sel(Write_Register));  // open: out8, out9, out10, out11, out12, out13, out14, out15
  and and_1 (and_1_out, decoder_1_out0, 1'b0);
  and and_2 (and_2_out, decoder_1_out1, Write_Signal);
  and and_3 (and_3_out, decoder_1_out2, Write_Signal);
  and and_4 (and_4_out, decoder_1_out3, Write_Signal);
  and and_5 (and_5_out, decoder_1_out4, Write_Signal);
  and and_6 (and_6_out, decoder_1_out5, Write_Signal);
  and and_7 (and_7_out, decoder_1_out6, Write_Signal);
  and and_8 (and_8_out, decoder_1_out7, Write_Signal);
  Multiplexer #(.enable("false")) multiplexer_1 (.in0(and_8_out), .in1(Clear), .out(multiplexer_1_out), .sel(Clear));
  Multiplexer #(.width(8), .enable("false")) multiplexer_2 (
    .in0(Write_Data), .in1({8{1'b1}}), .out(multiplexer_2_out), .sel(Clear));
  Register zero (.D(Write_Data), .en(and_1_out), .Q(zero_q), .clk(CLK), .clr(Clear));
  Register t0 (.D(Write_Data), .en(and_2_out), .Q(t0_q), .clk(CLK), .clr(Clear));
  Register t1 (.D(Write_Data), .en(and_3_out), .Q(t1_q), .clk(CLK), .clr(Clear));
  Register t2 (.D(Write_Data), .en(and_4_out), .Q(t2_q), .clk(CLK), .clr(Clear));
  Register t3 (.D(Write_Data), .en(and_5_out), .Q(t3_q), .clk(CLK), .clr(Clear));
  Register t4 (.D(Write_Data), .en(and_6_out), .Q(t4_q), .clk(CLK), .clr(Clear));
  Register t5 (.D(Write_Data), .en(and_7_out), .Q(t5_q), .clk(CLK), .clr(Clear));
  Register sp (.D(multiplexer_2_out), .en(multiplexer_1_out), .Q(sp_q), .clk(multiplexer_3_out));  // open: clr
  Multiplexer #(.enable("false")) multiplexer_3 (.in0(CLK), .in1(Clear), .out(multiplexer_3_out), .sel(Clear));
  Multiplexer #(.select(4), .width(8), .enable("false")) multiplexer_4 (
    .in0(zero_q), .in1(t0_q), .in2(t1_q), .in3(t2_q), .in4(t3_q), .in5(t4_q), .in6(t5_q), .in7(sp_q),
    .out(multiplexer_4_out), .sel(Read_Register_1));  // open: in8, in9, in10, in11, in12, in13, in14, in15
  Multiplexer #(.select(4), .width(8), .enable("false")) multiplexer_5 (
    .in0(zero_q), .in1(t0_q), .in2(t1_q), .in3(t2_q), .in4(t3_q), .in5(t4_q), .in6(t5_q), .in7(sp_q),
    .out(multiplexer_5_out), .sel(Read_Register_2));  // open: in8, in9, in10, in11, in12, in13, in14, in15
  and and_9 (and_9_out, comparator_1_eq, Write_Signal);
  Comparator #(.width(4)) comparator_1 (.a(Read_Register_1), .b(Write_Register), .eq(comparator_1_eq));  // open: gt, lt
  and and_10 (and_10_out, comparator_2_eq, Write_Signal);
  Comparator #(.width(4)) comparator_2 (.a(Read_Register_2), .b(Write_Register), .eq(comparator_2_eq));  // open: gt, lt
  Multiplexer #(.width(8), .enable("false")) multiplexer_6 (
    .in0(multiplexer_4_out), .in1(Write_Data), .out(Read_Data_1), .sel(and_9_out));
  Multiplexer #(.width(8), .enable("false")) multiplexer_7 (
    .in0(multiplexer_5_out), .in1(Write_Data), .out(Read_Data_2), .sel(and_10_out));

  // Other names for the same wires on the sheet: RD[3:0] = Write_Register; RegWrite = Write_Signal;
  //   RS[3:0] = Read_Register_1; RT[3:0] = Read_Register_2; WD[7:0] = Write_Data
endmodule
