// Logisim project Stack-Logic.circ as structural Verilog: 1 circuit, main circuit Stack Logic
module Stack_Logic (
  input  [3:0] Source_Reg_1,
  output Store_Stack
);

  wire not_1_out;

  not not_1 (not_1_out, Source_Reg_1[3]);
  and and_1 (Store_Stack, not_1_out, Source_Reg_1[2], Source_Reg_1[1], Source_Reg_1[0]);
endmodule
