// Logisim project control_hazard.circ as structural Verilog: 1 circuit, main circuit control_hazard
module control_hazard (
  input  bne,
  input  [3:0] EX_MEM_Rt,
  input  [3:0] IF_ID_Rs,
  input  [3:0] ID_EX_Rd,
  input  [3:0] IF_ID_Rt,
  input  beq,
  input  EX_MEM_MemRead,
  input  ID_EX_RegWrite,
  output jump_control
);

  wire Comp_with_ID_EX, Comp_with_Mem, comparator_1_eq, comparator_2_eq, comparator_3_eq, comparator_4_eq,
       or_1_out, or_2_out, or_3_out, or_4_out;

  Comparator #(.width(4)) comparator_1 (.a(EX_MEM_Rt), .b(IF_ID_Rs), .eq(comparator_1_eq));  // open: gt, lt
  Comparator #(.width(4)) comparator_2 (.a(ID_EX_Rd), .b(IF_ID_Rs), .eq(comparator_2_eq));  // open: gt, lt
  Comparator #(.width(4)) comparator_3 (.a(ID_EX_Rd), .b(IF_ID_Rt), .eq(comparator_3_eq));  // open: gt, lt
  Comparator #(.width(4)) comparator_4 (.a(EX_MEM_Rt), .b(IF_ID_Rt), .eq(comparator_4_eq));  // open: gt, lt
  or or_1 (or_1_out, comparator_1_eq, comparator_4_eq);
  or or_2 (or_2_out, comparator_2_eq, comparator_3_eq);
  and and_1 (Comp_with_Mem, or_1_out, EX_MEM_MemRead);
  and and_2 (Comp_with_ID_EX, or_2_out, ID_EX_RegWrite);
  or or_3 (or_3_out, bne, beq);
  or or_4 (or_4_out, Comp_with_Mem, Comp_with_ID_EX);
  and and_3 (jump_control, or_3_out, or_4_out);
endmodule
