// Logisim project SingleCycleMIPS.circ as structural Verilog: 3 circuits, main circuit main
module main (
  input  Reset
);

  wire ALUSrc, and_1_out, and_2_out, and_3_out, and_4_out, Beq, Bne, Clock, Jump, Load_Stack, MemRead,
       MemToReg, MemWrite, not_1_out, not_2_out, RegDst, RegWrite, Shift, Store_Stack, Zero;
  wire [2:0] ALUOp;
  wire [3:0] DstReg, multiplexer_1_out, OpCode, ShiftAmount, Source_Register_1, Source_Register_2;
  wire [7:0] Address_Immediate, ALU_Result, bit_extender_1_out, JumpAddress, multiplexer_2_out,
       multiplexer_3_out, multiplexer_4_out, New_PC, Old_PC, Read_Memory_Data, Read_Register_1,
       Read_Register_2, Read_Stack_Data, WriteData;
  wire [19:0] Instruction;

  Instruction_Memory instruction_memory_1 (
    .PC_input(New_PC), .Reset(Reset), .Clock(Clock), .Instruction(Instruction), .PC_Out(Old_PC));
  Multiplexer #(.width(4), .enable("false")) multiplexer_1 (
    .in0(Source_Register_2), .in1(DstReg), .out(multiplexer_1_out), .sel(RegDst));
  Next_PC_Calculation next_pc_calculation_1 (
    .Zero(Zero), .Beq(Beq), .Bne(Bne), .Branch_Target(Address_Immediate), .Jump(Jump),
    .Jump_Target(JumpAddress), .PC(Old_PC), .New_PC(New_PC));
  not not_1 (not_1_out, Load_Stack);
  and and_1 (and_1_out, MemRead, not_1_out);
  and and_2 (and_2_out, not_2_out, MemWrite);
  Data_Memory data_memory_1 (
    .Address(ALU_Result), .Write_Data(Read_Register_2), .Mem_Write(and_2_out), .Mem_Read(and_1_out),
    .Clear(Reset), .Data(Read_Memory_Data), .CLK(Clock));
  Register_File register_file_1 (
    .Read_Register_1(Source_Register_1), .Read_Register_2(Source_Register_2),
    .Write_Register(multiplexer_1_out), .Write_Data(WriteData), .Read_Data_1(Read_Register_1),
    .Read_Data_2(Read_Register_2), .Write_Signal(RegWrite), .CLK(Clock), .Clear(Reset));
  not not_2 (not_2_out, Store_Stack);
  insSplitter inssplitter_1 (
    .in_1(Instruction), .Shift_Amount(ShiftAmount), .Dst_Reg(DstReg), .Src_Reg2(Source_Register_2),
    .Src_Reg1(Source_Register_1), .Opcode(OpCode), .Address_Immediate(Address_Immediate),
    .Target_Jump_Address(JumpAddress));
  assign bit_extender_1_out = {{4{1'b0}}, ShiftAmount};  // Bit_Extender bit_extender_1
  Stack_Logic stack_logic_1 (
    .Source_Reg_1(Source_Register_1), .Source_Reg_2(Source_Register_2), .Load_Stack(Load_Stack),
    .Store_Stack(Store_Stack));
  and and_3 (and_3_out, MemRead, Load_Stack);
  Multiplexer #(.width(8), .enable("false")) multiplexer_2 (
    .in0(Read_Register_1), .in1(bit_extender_1_out), .out(multiplexer_2_out), .sel(Shift));
  Multiplexer #(.select(2), .width(8), .enable("false")) multiplexer_3 (
    .in0(Read_Register_2), .in1(Address_Immediate), .in2(Read_Register_1), .out(multiplexer_3_out),
    .sel({Shift, ALUSrc}));  // open: in3
  and and_4 (and_4_out, Store_Stack, MemWrite);
  Stack_Memory stack_memory_1 (
    .Address(ALU_Result), .Write_Data(Read_Register_2), .Mem_Write(and_4_out), .Mem_Read(and_3_out),
    .Clear(Reset), .Data(Read_Stack_Data), .CLK(Clock));
  Control_Unit control_unit_1 (
    .Opcode(OpCode), .Shift(Shift), .ALU_Op(ALUOp), .Reg_Dest(RegDst), .ALU_Src(ALUSrc), .MemToReg(MemToReg),
    .RegWrite(RegWrite), .beq(Beq), .bneq(Bne), .MemWrite(MemWrite), .MemRead(MemRead), .Jump(Jump));
  // ALU_8_by_ART alu_8_by_art_1: pin names not known; wires that end beside it: multiplexer_2_out, multiplexer_3_out, ALUOp, Zero, ALU_Result
  Clock u_Clock (.out(Clock));
  Multiplexer #(.width(8), .enable("false")) multiplexer_4 (
    .in0(Read_Memory_Data), .in1(Read_Stack_Data), .out(multiplexer_4_out), .sel(Load_Stack));
  Multiplexer #(.width(8), .enable("false")) multiplexer_5 (
    .in0(ALU_Result), .in1(multiplexer_4_out), .out(WriteData), .sel(MemToReg));
endmodule

module Next_PC_Calculation (
  input  Zero,
  input  Beq,
  input  Bne,
  input  [7:0] Branch_Target,
  input  Jump,
  input  [7:0] Jump_Target,
  input  [7:0] PC,
  output [7:0] New_PC
);

  wire Branch;
  wire [7:0] New_Branch_Target, PC___1, Temp_PC;

  // ALU_8_by_ART alu_8_by_art_1: pin names not known; wires that end beside it: PC, 8'h1, 3'b000, PC___1
  Multiplexer #(.enable("false")) multiplexer_1 (.in0(Bne), .in1(Beq), .out(Branch), .sel(Zero));
  // ALU_8_by_ART alu_8_by_art_2: pin names not known; wires that end beside it: Branch_Target, PC___1, 3'b000, New_Branch_Target
  Multiplexer #(.width(8), .enable("false")) multiplexer_2 (
    .in0(PC___1), .in1(New_Branch_Target), .out(Temp_PC), .sel(Branch));
  Multiplexer #(.width(8), .enable("false")) multiplexer_3 (.in0(Temp_PC), .in1(Jump_Target), .out(New_PC), .sel(Jump));
endmodule

module Register_File (
  input  [3:0] Read_Register_1,
  input  [3:0] Read_Register_2,
  input  [3:0] Write_Register,
  input  [7:0] Write_Data,
  input  Write_Signal,
  input  CLK,
  input  Clear,
  output [7:0] Read_Data_1,
  output [7:0] Read_Data_2
);

  wire and_1_out, and_2_out, and_3_out, and_4_out, and_5_out, and_6_out, and_7_out, and_8_out,
       decoder_1_out0, decoder_1_out1, decoder_1_out2, decoder_1_out3, decoder_1_out4, decoder_1_out5,
       decoder_1_out6, decoder_1_out7, multiplexer_1_out, multiplexer_3_out;
  wire [7:0] multiplexer_2_out, sp_q, t0_q, t1_q, t2_q, t3_q, t4_q, t5_q, zero_q;

  Decoder #(.select(4), .enable("false")) decoder_1 (
    .out0(decoder_1_out0), .out1(decoder_1_out1), .out2(decoder_1_out2), .out3(decoder_1_out3),
    .out4(decoder_1_out4), .out5(decoder_1_out5), .out6(decoder_1_out6), .out7(decoder_1_out7),
    .sel(Write_Register));  // open: out8, out9, out10, out11, out12, out13, out14, out15
  and and_1 (and_1_out, decoder_1_out0, 1'b0);
  and and_2 (and_2_out, decoder_1_out1, Write_Signal);
  and and_3 (and_3_out, decoder_1_out2, Write_Signal);
  and and_4 (and_4_out, decoder_1_out3, Write_Signal);
  and and_5 (and_5_out, decoder_1_out4, Write_Signal);
  and and_6 (and_6_out, decoder_1_out5, Write_Signal);
  and and_7 (and_7_out, decoder_1_out6, Write_Signal);
  and and_8 (and_8_out, decoder_1_out7, Write_Signal);
  Multiplexer #(.enable("false")) multiplexer_1 (.in0(and_8_out), .in1(Clear), .out(multiplexer_1_out), .sel(Clear));
  Multiplexer #(.width(8), .enable("false")) multiplexer_2 (
    .in0(Write_Data), .in1({8{1'b1}}), .out(multiplexer_2_out), .sel(Clear));
  Register zero (.D(Write_Data), .en(and_1_out), .Q(zero_q), .clk(CLK), .clr(Clear));
  Register t0 (.D(Write_Data), .en(and_2_out), .Q(t0_q), .clk(CLK), .clr(Clear));
  Register t1 (.D(Write_Data), .en(and_3_out), .Q(t1_q), .clk(CLK), .clr(Clear));
  Register t2 (.D(Write_Data), .en(and_4_out), .Q(t2_q), .clk(CLK), .clr(Clear));
  Register t3 (.D(Write_Data), .en(and_5_out), .Q(t3_q), .clk(CLK), .clr(Clear));
  Register t4 (.D(Write_Data), .en(and_6_out), .Q(t4_q), .clk(CLK), .clr(Clear));
  Register t5 (.D(Write_Data), .en(and_7_out), .Q(t5_q), .clk(CLK), .clr(Clear));
  Register sp (.D(multiplexer_2_out), .en(multiplexer_1_out), .Q(sp_q), .clk(multiplexer_3_out));  // open: clr
  Multiplexer #(.enable("false")) multiplexer_3 (.in0(CLK), .in1(Clear), .out(multiplexer_3_out), .sel(Clear));
  Multiplexer #(.select(4), .width(8), .enable("false")) multiplexer_4 (
    .in0(zero_q), .in1(t0_q), .in2(t1_q), .in3(t2_q), .in4(t3_q), .in5(t4_q), .in6(t5_q), .in7(sp_q),
    .out(Read_Data_1), .sel(Read_Register_1));  // open: in8, in9, in10, in11, in12, in13, in14, in15
  Multiplexer #(.select(4), .width(8), .enable("false")) multiplexer_5 (
    .in0(zero_q), .in1(t0_q), .in2(t1_q), .in3(t2_q), .in4(t3_q), .in5(t4_q), .in6(t5_q), .in7(sp_q),
    .out(Read_Data_2), .sel(Read_Register_2));  // open: in8, in9, in10, in11, in12, in13, in14, in15
endmodule
