// Logisim project Stack-Logic.circ as structural Verilog: 1 circuit, main circuit Stack Logic
module Stack_Logic (
  input  [3:0] Source_Reg_1,
  input  [3:0] Source_Reg_2,
  output Load_Stack,
  output Store_Stack
);

  wire not_1_out, not_2_out;

  not not_1 (not_1_out, Source_Reg_1[3]);
  not not_2 (not_2_out, Source_Reg_2[3]);
  and and_1 (Load_Stack, not_1_out, Source_Reg_1[2], Source_Reg_1[1], Source_Reg_1[0]);
  // AND_Gate and_2 has open pins: in0=not_2_out, in1=Source_Reg_2[2], in2=Source_Reg_2[1], in3=Source_Reg_2[0], out=open

  assign Store_Stack = Load_Stack;
endmodule
