// Logisim project rwd.circ as structural Verilog: 3 circuits, main circuit Instruction Memory
module Instruction_Memory (
  input  [7:0] PC_input,
  input  Reset,
  input  Clock,
  output [7:0] PC_Out,
  output [19:0] Instruction
);

  Register register_1 (.D(PC_input), .en(1'b1), .Q(PC_Out), .clk(Clock), .clr(Reset));
  ROM #(.dataWidth(20)) rom_1 (.addr(PC_Out), .data(Instruction), .sel(1'b1));

  // Other names for the same wires on the sheet: Clk = Clock; Ins[19:0] = Instruction; PC_Val[7:0] = PC_input;
  //   Res = Reset
endmodule

module insSplitter (
  input  [19:0] in_1,
  output [3:0] Shift_Amount,
  output [3:0] Dst_Reg,
  output [3:0] Src_Reg2,
  output [3:0] Src_Reg1,
  output [3:0] Opcode,
  output [7:0] Address_Immediate,
  output [7:0] Target_Jump_Address
);


  assign Address_Immediate = in_1[7:0];
  assign Dst_Reg = in_1[7:4];
  assign Opcode = in_1[19:16];
  assign Shift_Amount = in_1[3:0];
  assign Src_Reg1 = in_1[15:12];
  assign Src_Reg2 = in_1[11:8];
  assign Target_Jump_Address = in_1[15:8];

  // Other names for the same wires on the sheet: Ins[19:0] = in_1; shift[3:0] = in_1[3:0]
endmodule

module Control_Unit (
  input  [3:0] Opcode,
  output Shift,
  output [2:0] ALU_Op,
  output Reg_Dest,
  output ALU_Src,
  output MemToReg,
  output RegWrite,
  output beq,
  output bneq,
  output MemWrite,
  output MemRead,
  output Jump
);

  wire [3:1] rom_1_data;

  ROM #(.addrWidth(4), .dataWidth(16)) rom_1 (
    .addr(Opcode),
    .data({Jump, MemRead, MemWrite, bneq, beq, RegWrite, MemToReg, ALU_Src, Reg_Dest, ALU_Op, rom_1_data, Shift}),
    .sel(1'b1));
endmodule
